// Logisim project cache.circ as structural Verilog: 2 circuits, main circuit cache-entry
module main (
  input  [7:0] address,
  input  read_enable,
  input  [31:0] ROM_data_in,
  output [7:0] data_out,
  output [5:0] ROM_read_address,
  output ROM_read_enable
);

  wire cache_entry_1_miss, cache_entry_2_miss, cache_entry_3_miss, cache_entry_4_miss, demultiplexer_2_out0,
       demultiplexer_2_out1, demultiplexer_2_out2, demultiplexer_2_out3, multiplexer_1_out;
  wire [3:0] demultiplexer_1_out0, demultiplexer_1_out1, demultiplexer_1_out2, demultiplexer_1_out3;
  wire [7:0] multiplexer_3_out, multiplexer_4_out;
  wire [31:0] cache_entry_1_data_out, cache_entry_2_data_out, cache_entry_3_data_out, cache_entry_4_data_out,
       multiplexer_2_out;

  Demultiplexer #(.select(2), .width(4), .enable("false")) demultiplexer_1 (
    .out0(demultiplexer_1_out0), .out1(demultiplexer_1_out1), .out2(demultiplexer_1_out2),
    .out3(demultiplexer_1_out3), .in(address[7:4]), .sel(address[3:2]));
  Demultiplexer #(.select(2), .enable("false")) demultiplexer_2 (
    .out0(demultiplexer_2_out0), .out1(demultiplexer_2_out1), .out2(demultiplexer_2_out2),
    .out3(demultiplexer_2_out3), .in(ROM_read_enable), .sel(address[3:2]));
  cache_entry cache_entry_1 (
    .tag(demultiplexer_1_out0), .clock(demultiplexer_2_out0), .data_out(cache_entry_1_data_out),
    .miss(cache_entry_1_miss));  // open: data_in
  cache_entry cache_entry_2 (
    .tag(demultiplexer_1_out1), .clock(demultiplexer_2_out1), .data_out(cache_entry_2_data_out),
    .miss(cache_entry_2_miss));  // open: data_in
  cache_entry cache_entry_3 (
    .tag(demultiplexer_1_out2), .clock(demultiplexer_2_out2), .data_out(cache_entry_3_data_out),
    .miss(cache_entry_3_miss));  // open: data_in
  cache_entry cache_entry_4 (
    .tag(demultiplexer_1_out3), .clock(demultiplexer_2_out3), .data_out(cache_entry_4_data_out),
    .miss(cache_entry_4_miss));  // open: data_in
  and and_1 (ROM_read_enable, read_enable, multiplexer_1_out);
  Multiplexer #(.select(2), .enable("false")) multiplexer_1 (
    .in0(cache_entry_1_miss), .in1(cache_entry_2_miss), .in2(cache_entry_3_miss), .in3(cache_entry_4_miss),
    .out(multiplexer_1_out), .sel(address[3:2]));
  Multiplexer #(.select(2), .width(32), .enable("false")) multiplexer_2 (
    .in0(cache_entry_1_data_out), .in1(cache_entry_2_data_out), .in2(cache_entry_3_data_out),
    .in3(cache_entry_4_data_out), .out(multiplexer_2_out), .sel(address[3:2]));
  Multiplexer #(.select(2), .width(8), .enable("false")) multiplexer_3 (
    .in0(multiplexer_2_out[7:0]), .in1(multiplexer_2_out[15:8]), .in2(multiplexer_2_out[23:16]),
    .in3(multiplexer_2_out[31:24]), .out(multiplexer_3_out), .sel(address[1:0]));
  Multiplexer #(.select(2), .width(8), .enable("false")) multiplexer_4 (
    .in0(ROM_data_in[7:0]), .in1(ROM_data_in[15:8]), .in2(ROM_data_in[23:16]), .in3(ROM_data_in[31:24]),
    .out(multiplexer_4_out), .sel(ROM_read_address[1:0]));
  Multiplexer #(.width(8), .enable("false")) multiplexer_5 (
    .in0(multiplexer_3_out), .in1(multiplexer_4_out), .out(data_out), .sel(ROM_read_enable));
  // Pins of 2 and 6 bits meet at ROM_read_address

  // Notes on the sheet:
  //   data_out: pull=down
  //   ROM_read_address: pull=down
  //   ROM_read_enable: pull=down
  //   byte offset
  //   index
  //   tag
endmodule

module cache_entry (
  input  [31:0] data_in,
  input  [3:0] tag,
  input  clock,
  output [31:0] data_out,
  output miss
);

  wire and_1_out, comparator_1_eq, valid_q;
  wire [3:0] tagreg_q;

  Register #(.width(32), .trigger("falling")) cache (.D(data_in), .en(miss), .Q(data_out), .clk(clock));  // open: clr
  Register #(.width(4), .trigger("falling")) tagreg (.D(tag), .en(miss), .Q(tagreg_q), .clk(clock));  // open: clr
  Register #(.width(1), .trigger("falling")) valid (.D(1'b1), .en(miss), .Q(valid_q), .clk(clock));  // open: clr
  Comparator #(.width(4)) comparator_1 (.a(tagreg_q), .b(tag), .eq(comparator_1_eq));  // open: gt, lt
  and and_1 (and_1_out, comparator_1_eq, valid_q);
  not not_1 (miss, and_1_out);
endmodule
